# Fritzing sketch modelo-fritzing (saved by Fritzing 0.9.3b)
breadboards: 1

parts:
  Componente1 = Arduino Uno (Rev3)
  R1 = Photocell (LDR) [package=THT]  # not connected
  R2 = Photocell (LDR) [package=THT]  # not connected
  4_Channel_Relay1 = 4 Channel Power Relay
  LD1 = LD
  LD2 = LD
  S1 = Reed switch [package=THT]  # not connected
  S2 = SWITCH-MOMENTARY-2 [package=reed_switch_pth]  # not connected

nets:
  N1: Componente1.D12/MISO, 4_Channel_Relay1.IN2
  N2: Componente1.D13/SCK, 4_Channel_Relay1.IN1
  GND: Componente1.GND, 4_Channel_Relay1.GND, LD1.cathode, LD2.cathode
  5V: Componente1.5V, 4_Channel_Relay1.VCC

custom parts:
  4 Channel Power Relay: A 4 channel power relay. The module operates at 5V.
  LD: A Generic Red Dot Laser Diode Module (~5mW)
